# Fritzing sketch schematic (saved by Fritzing 0.9.4)

parts:
  WeMos_D1_Mini1 = WeMos D1 Mini
  WeMos_D1_Mini_Relay_Shield_V1 = WeMos D1 Mini Relay Shield V2
  WeMos_D1_Mini_Protoboard_Shield1 = WeMos D1 Mini Protoboard Shield
  DS1 = DS18B20 1-Wire Temperature Sensor [part_number=DS18B20]
  R1 = Resistor [tolerance=±5% resistance=4.7k package="0805 [SMD]"]  # not connected

nets:
  3V3: WeMos_D1_Mini1.3V3, WeMos_D1_Mini_Protoboard_Shield1.3V3
  5V: WeMos_D1_Mini1.5V, WeMos_D1_Mini_Relay_Shield_V1.5V
  N1: WeMos_D1_Mini1.D5, WeMos_D1_Mini_Relay_Shield_V1.D1
  N2: WeMos_D1_Mini1.D6, WeMos_D1_Mini_Protoboard_Shield1.D6, DS1.DQ
  N3: WeMos_D1_Mini1.G, WeMos_D1_Mini_Relay_Shield_V1.G
  N4: WeMos_D1_Mini_Protoboard_Shield1.G, DS1.GND
  N5: WeMos_D1_Mini_Protoboard_Shield1.X3-Y8, DS1.VDD

notes:
  D1 interfered with OneWire and changed to D5
